# Fritzing sketch CircuitPython_Distance_Sensor_Fritzing (saved by Fritzing 0.9.3b)

parts:
  Part1 = Adafruit Metro M0 Express
  HC-SR04_Sensor_1 = HC-SR04 Ultrasonic Distance Sensor

nets:
  N1: Part1.D10, HC-SR04_Sensor_1.TRIG
  N2: Part1.D7, HC-SR04_Sensor_1.ECHO
  +5V: Part1.+5V, HC-SR04_Sensor_1.VCC
  GND: Part1.GND, HC-SR04_Sensor_1.GND

custom parts:
  Adafruit Metro M0 Express: Metro is our series of microcontroller boards for use with the Arduino IDE. This new Metro board looks a whole lot like our original Metro 328, but with a huge upgrade. Instead of the ATmega328, this Metro features a ATSAMD21G18 chip, an ARM Cortex M0+. It's our first Metro that is designed for use with CircuitPython! CircuitPython is our beginner-oriented flavor of MicroPython - and as the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
