# Fritzing sketch CircuitPython_LCD_Fritzing (saved by Fritzing 0.9.3b)
breadboards: 1

parts:
  Part1 = Adafruit Metro M0 Express
  LCD_Backpack1 = LCD Backpack [part_number="LCM1602 IIC" chip_label="LCM1602 IIC" package="DIP (Dual Inline) [THT]"]
  LCD1 = LCD screen
  S1 = Pushbutton [package="[THT]"]
  S2 = Toggle Switch [package=THT]

nets:
  N1: Part1.SCL, LCD_Backpack1.SCL
  N2: Part1.SDA, LCD_Backpack1.SDA
  N3: Part1.D8, S2.L2
  N4: Part1.D4, S1.Pin_3, S1.Pin_4
  +5V: Part1.+5V, LCD_Backpack1.VCC, S2.COM
  GND: Part1.GND, LCD_Backpack1.GND, S1.Pin_1, S1.Pin_2
  VSS: LCD_Backpack1.VSS, LCD1.VSS
  VDD: LCD_Backpack1.VDD, LCD1.VDD
  N5: LCD_Backpack1.V0, LCD1.V0
  N6: LCD_Backpack1.RS, LCD1.RS
  N7: LCD_Backpack1.RW, LCD1.R/W
  N8: LCD_Backpack1.E, LCD1.E
  N9: LCD_Backpack1.D0, LCD1.DB0
  N10: LCD_Backpack1.D1, LCD1.DB1
  N11: LCD_Backpack1.D2, LCD1.DB2
  N12: LCD_Backpack1.D3, LCD1.DB3
  N13: LCD_Backpack1.D4, LCD1.DB4
  N14: LCD_Backpack1.D5, LCD1.DB5
  N15: LCD_Backpack1.D6, LCD1.DB6
  N16: LCD_Backpack1.D7, LCD1.DB7
  N17: LCD_Backpack1.A, LCD1.LED+
  N18: LCD_Backpack1.K, LCD1.LED-

custom parts:
  Adafruit Metro M0 Express: Metro is our series of microcontroller boards for use with the Arduino IDE. This new Metro board looks a whole lot like our original Metro 328, but with a huge upgrade. Instead of the ATmega328, this Metro features a ATSAMD21G18 chip, an ARM Cortex M0+. It's our first Metro that is designed for use with CircuitPython! CircuitPython is our beginner-oriented flavor of MicroPython - and as the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
  LCD Backpack: I2C-Module to use a 1602 or 2004 LCD on with the wire.h library Serial LCD Modul
