# Fritzing sketch CircuitPython_PhotoInterrupters_Fritzing (saved by Fritzing 0.9.3b)
breadboards: 1

parts:
  Part1 = Adafruit Metro M0 Express
  LCD1 = LCD screen
  LCD_Backpack1 = LCD Backpack [part_number="LCM1602 IIC" chip_label="LCM1602 IIC" package="DIP (Dual Inline) [THT]"]
  U1 = Photointerrupter [package=cnz1120]

nets:
  N1: Part1.SCL, LCD_Backpack1.SCL
  N2: Part1.SDA, LCD_Backpack1.SDA
  N3: Part1.D8, U1.1
  +5V: Part1.+5V, LCD_Backpack1.VCC, U1.3
  GND: Part1.GND, LCD_Backpack1.GND, U1.2
  VSS: LCD1.VSS, LCD_Backpack1.VSS
  VDD: LCD1.VDD, LCD_Backpack1.VDD
  N4: LCD1.V0, LCD_Backpack1.V0
  N5: LCD1.RS, LCD_Backpack1.RS
  N6: LCD1.R/W, LCD_Backpack1.RW
  N7: LCD1.E, LCD_Backpack1.E
  N8: LCD1.DB0, LCD_Backpack1.D0
  N9: LCD1.DB1, LCD_Backpack1.D1
  N10: LCD1.DB2, LCD_Backpack1.D2
  N11: LCD1.DB3, LCD_Backpack1.D3
  N12: LCD1.DB4, LCD_Backpack1.D4
  N13: LCD1.DB5, LCD_Backpack1.D5
  N14: LCD1.DB6, LCD_Backpack1.D6
  N15: LCD1.DB7, LCD_Backpack1.D7
  N16: LCD1.LED+, LCD_Backpack1.A
  N17: LCD1.LED-, LCD_Backpack1.K

custom parts:
  Adafruit Metro M0 Express: Metro is our series of microcontroller boards for use with the Arduino IDE. This new Metro board looks a whole lot like our original Metro 328, but with a huge upgrade. Instead of the ATmega328, this Metro features a ATSAMD21G18 chip, an ARM Cortex M0+. It's our first Metro that is designed for use with CircuitPython! CircuitPython is our beginner-oriented flavor of MicroPython - and as the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
  LCD Backpack: I2C-Module to use a 1602 or 2004 LCD on with the wire.h library Serial LCD Modul
  Photointerrupter: LED-to-NPN optoisolator
